// Digital circuit pipelinedMult.dig as structural Verilog
module pipelinedMult (
  input  rst,
  input  Clk,
  input  valid_in,
  input  [7:0] A,
  input  [7:0] B,
  output [15:0] result,
  output valid_out
);

  wire add_1_c_o, add_2_c_o, add_3_c_o, add_4_c_o, add_6_c_o, not_2_out, nrst, stage1_valid, stage2_valid,
       stage3_valid, Test___nInput_out;
  wire [7:0] A_t, B_t, counter_1_out, stage1_a, stage1_b, stage2_a;
  wire [15:0] add_1_s, add_2_s, add_3_s, add_4_s, add_6_s, multiplexer_1_out, multiplexer_2_out,
       multiplexer_3_out, multiplexer_4_out, multiplexer_5_out, multiplexer_6_out, multiplexer_7_out,
       multiplexer_8_out, stage2_partial, stage3_sum, temp1, temp2;

  not not_1 (nrst, rst);
  Counter #(.Bits(8)) counter_1 (.en(1'b1), .C(Clk), .clr(1'b0), .out(counter_1_out));  // open: ovf
  DipSwitch Test___nInput (.out(Test___nInput_out));
  not not_2 (not_2_out, Test___nInput_out);
  // Probe A = B on counter_1_out
  assign A_t = not_2_out ? counter_1_out : 8'bz;  // Driver driver_1
  assign A_t = Test___nInput_out ? A : 8'bz;  // Driver driver_2
  assign B_t = Test___nInput_out ? B : 8'bz;  // Driver driver_3
  assign B_t = not_2_out ? counter_1_out : 8'bz;  // Driver driver_4
  Register #(.Bits(8)) u_stage1_a (.D(A_t), .C(Clk), .en(nrst), .Q(stage1_a));
  Register #(.Bits(8)) u_stage1_b (.D(B_t), .C(Clk), .en(nrst), .Q(stage1_b));
  Register u_stage1_valid (.D(valid_in), .C(Clk), .en(nrst), .Q(stage1_valid));
  Register #(.Bits(16)) u_stage2_partial (.D(temp1), .C(Clk), .en(nrst), .Q(stage2_partial));
  Register #(.Bits(8)) stage2_b (.D(stage1_a), .C(Clk), .en(nrst), .Q(stage2_a));
  Register #(.Bits(8)) stage2_b_2 (.D(stage1_b), .C(Clk), .en(nrst), .Q(stage2_a));
  Register u_stage2_valid (.D(stage1_valid), .C(Clk), .en(nrst), .Q(stage2_valid));
  Multiplexer #(.Bits(16)) multiplexer_1 (
    .sel(stage1_a[0]), .in_0({16{1'b0}}), .in_1({{8{1'b0}}, stage1_b}), .out(multiplexer_1_out));
  Multiplexer #(.Bits(16)) multiplexer_2 (
    .sel(stage1_a[1]), .in_0({16{1'b0}}), .in_1({{7{1'b0}}, stage1_b, 1'b0}), .out(multiplexer_2_out));
  Multiplexer #(.Bits(16)) multiplexer_3 (
    .sel(stage1_a[2]), .in_0({16{1'b0}}), .in_1({{6{1'b0}}, stage1_b, 2'b00}), .out(multiplexer_3_out));
  Multiplexer #(.Bits(16)) multiplexer_4 (
    .sel(stage1_a[3]), .in_0({16{1'b0}}), .in_1({{5{1'b0}}, stage1_b, 3'b000}), .out(multiplexer_4_out));
  Multiplexer #(.Bits(16)) multiplexer_5 (
    .sel(stage2_a[4]), .in_0({16{1'b0}}), .in_1({4'b0000, stage2_a, 4'b0000}), .out(multiplexer_5_out));
  Multiplexer #(.Bits(16)) multiplexer_6 (
    .sel(stage2_a[5]), .in_0({16{1'b0}}), .in_1({3'b000, stage2_a, {5{1'b0}}}), .out(multiplexer_6_out));
  Multiplexer #(.Bits(16)) multiplexer_7 (
    .sel(stage2_a[6]), .in_0({16{1'b0}}), .in_1({2'b00, stage2_a, {6{1'b0}}}), .out(multiplexer_7_out));
  Multiplexer #(.Bits(16)) multiplexer_8 (
    .sel(stage2_a[7]), .in_0({16{1'b0}}), .in_1({1'b0, stage2_a, {7{1'b0}}}), .out(multiplexer_8_out));
  Add #(.Bits(16)) add_1 (.a(multiplexer_1_out), .b(multiplexer_2_out), .c_i(1'b0), .s(add_1_s), .c_o(add_1_c_o));
  Add #(.Bits(16)) add_2 (.a(multiplexer_5_out), .b(multiplexer_6_out), .c_i(1'b0), .s(add_2_s), .c_o(add_2_c_o));
  Register #(.Bits(16)) u_stage3_sum (.D(temp2), .C(Clk), .en(nrst), .Q(stage3_sum));
  Register u_Stage3_valid (.D(stage2_valid), .C(Clk), .en(nrst), .Q(stage3_valid));
  Add #(.Bits(16)) add_3 (.a(add_1_s), .b(multiplexer_3_out), .c_i(add_1_c_o), .s(add_3_s), .c_o(add_3_c_o));
  Add #(.Bits(16)) add_4 (.a(add_2_s), .b(multiplexer_7_out), .c_i(add_2_c_o), .s(add_4_s), .c_o(add_4_c_o));
  Add #(.Bits(16)) add_5 (.a(add_3_s), .b(multiplexer_4_out), .c_i(add_3_c_o), .s(temp1));  // open: c_o
  Add #(.Bits(16)) add_6 (.a(add_4_s), .b(multiplexer_8_out), .c_i(add_4_c_o), .s(add_6_s), .c_o(add_6_c_o));
  Register #(.Bits(16)) stage4_result (.D(stage3_sum), .C(Clk), .en(nrst), .Q(result));
  Register Stage4_valid (.D(stage3_valid), .C(Clk), .en(nrst), .Q(valid_out));
  Add #(.Bits(16)) add_7 (.a(add_6_s), .b(stage2_partial), .c_i(add_6_c_o), .s(temp2));  // open: c_o

  // Other names for the same wires on the sheet: stage2_b4 = stage2_a[4]; stage2_b5 = stage2_a[5];
  //   stage2_b6 = stage2_a[6]; stage2_b7 = stage2_a[7]; stage4_result[15:0] = result; stage4_valid = valid_out

  // Notes on the sheet:
  //   valid_in: default 1
  //   DEBUG
  //   INPUTS
  //   STAGE 1
  //   PARTIAL SUM GENERATION
  //   STAGE 2
  //   STAGE 3
  //   STAGE 4
  //   OUTPUTS
endmodule
